# Fritzing sketch smartdustbin (saved by Fritzing 0.9.4)

parts:
  Part1 = HX711 Weighing Sensor Module
  Load_Cell1 = Load Cell - Red/white/black/green
  hc-sr1 = hc-sr04
  U1 = NodeMCU V1.0
  Part2 = u-blox NEO-6M GPS Breakout

nets:
  VCC: Part1.VCC, hc-sr1.VCC, U1.3V3, Part2.VCC
  GND: Part1.GND, hc-sr1.GND, U1.GND, Part2.GND
  N1: Part1.DO/RX, U1.D5
  N2: Part1.CK/TX, U1.D6
  N3: Part1.E+, Load_Cell1.wire1
  N4: Part1.E-, Load_Cell1.wire3
  N5: Part1.A+, Load_Cell1.wire2
  N6: Part1.A-, Load_Cell1.wire4
  N7: hc-sr1.Trig, U1.D4
  N8: hc-sr1.Echo, U1.D3
  N9: U1.D1, Part2.RXD
  N10: U1.D2, Part2.TXD

custom parts:
  Load Cell - Red/white/black/green: A rectangle load cell/weighting pressure Sensor with four wires - Red, white, black, green. Normally corresponding with E+, E-, A+, A- respectively.
  NodeMCU V1.0: ESP8266 based NodeMCU
